# Fritzing sketch primo (saved by Fritzing 0.9.3b)
circuit board: 17.5878cm x 12.8072cm
breadboards: 1

parts:
  ESP01 = ESP8266 WiFi Module [part_number=ESP8266]
  Mega = Arduino Mega 2560 (Rev3)
  3V = Header 2 [package=screwterminal-3.5mm-2_lock]
  5V = Header 2 [package=screwterminal-3.5mm-2_lock]
  RHT1 = Humidity and Temperature Sensor RHT03
  LogicConv = Logic Level Converter
  Rele2 = 2-Channel 5v Relay Shield [package=relay-2ch5v10a]
  12v = Header 2 [package=screwterminal-3.5mm-2_lock]

nets:
  N1: ESP01.RXD, LogicConv.TX_LV
  N2: ESP01.VCC, ESP01.CH_PD, 3V.2, LogicConv.LV
  GND: ESP01.GND, Mega.GND, 3V.1, 5V.1, RHT1.GND_1, LogicConv.GND, Rele2.GND
  N3: ESP01.TXD, LogicConv.RX_LV
  N4: Mega.D15/RX3, Mega.D14/TX3
  N5: Mega.5V, Rele2.IN1
  N6: Mega.D2_PWM, LogicConv.TX_HV
  N7: Mega.D3_PWM, LogicConv.RX_HV
  N8: Mega.D4_PWM, RHT1.Data-signal
  N9: Mega.D23, Rele2.IN2
  VCC: 5V.2, RHT1.Vcc, LogicConv.HV, Rele2.VCC
  N10: Rele2.K2-In, Rele2.K2-Off, Rele2.K2-On
  N11: Rele2.JD-GND, 12v.1

custom parts:
  ESP8266 WiFi Module: Generic WiFi Module based on the ESP8266 with onboard PCB antenna and UART communications
  2-Channel 5v Relay Shield: 2 Channel 5v Relay Shield w. 2x SPD-06VDC-SD-C
